// Logisim project COMPUTER.circ as structural Verilog
module ADDITION (
  input  in_1,
  input  in_2,
  input  in_3,
  output out_4,
  output out_5
);

  wire and_1_out, and_2_out, xor_1_out;

  xor xor_1 (xor_1_out, in_1, in_2);
  and and_1 (and_1_out, in_2, in_1);
  xor xor_2 (out_4, in_3, xor_1_out);
  and and_2 (and_2_out, xor_1_out, in_3);
  or or_1 (out_5, and_2_out, and_1_out);
endmodule

module _4bit_ADDITION (
  input  in_1,
  input  in_2,
  input  in_3,
  input  in_4,
  input  in_5,
  input  in_6,
  input  in_7,
  input  in_8,
  input  in_9,
  output out_10,
  output out_11,
  output out_12,
  output out_13,
  output out_14
);

  wire addition_1_out_5, addition_2_out_5, addition_3_out_5;

  ADDITION addition_1 (.in_1(in_4), .in_2(in_8), .in_3(in_9), .out_4(out_13), .out_5(addition_1_out_5));
  ADDITION addition_2 (.in_1(in_3), .in_2(in_7), .in_3(addition_1_out_5), .out_4(out_12), .out_5(addition_2_out_5));
  ADDITION addition_3 (.in_1(in_2), .in_2(in_6), .in_3(addition_2_out_5), .out_4(out_11), .out_5(addition_3_out_5));
  ADDITION addition_4 (.in_1(in_1), .in_2(in_5), .in_3(addition_3_out_5), .out_4(out_10), .out_5(out_14));
endmodule

module ALU (
  input  in_1,
  input  in_2,
  input  in_3,
  input  in_4,
  input  in_5,
  input  in_6,
  input  in_7,
  input  in_8,
  input  in_9,
  output out_10,
  output out_11,
  output out_12,
  output out_13,
  output out_14,
  output out_15,
  output out_16
);

  wire and_1_out, and_2_out, not_1_out, not_2_out, not_3_out, not_4_out, xor_1_out, xor_2_out, xor_3_out,
       xor_4_out;

  xor xor_1 (xor_1_out, in_5, in_9);
  xor xor_2 (xor_2_out, in_6, in_9);
  xor xor_3 (xor_3_out, in_7, in_9);
  xor xor_4 (xor_4_out, in_8, in_9);
  _4bit_ADDITION u_4bit_addition_1 (
    .in_1(in_1), .in_2(in_2), .in_3(in_3), .in_4(in_4), .in_5(xor_1_out), .in_6(xor_2_out), .in_7(xor_3_out),
    .in_8(xor_4_out), .in_9(in_9), .out_10(out_10), .out_11(out_11), .out_12(out_12), .out_13(out_13),
    .out_14(out_14));
  not not_1 (not_1_out, out_10);
  not not_2 (not_2_out, out_11);
  not not_3 (not_3_out, out_12);
  not not_4 (not_4_out, out_13);
  and and_1 (and_1_out, not_1_out, not_2_out);
  and and_2 (and_2_out, and_1_out, not_3_out, not_3_out);
  and and_3 (out_16, and_2_out, not_4_out);

  assign out_15 = out_10;
endmodule
