// Logisim project STORAGE.circ as structural Verilog
module Data_Latch (
  input  in_1,
  input  in_2,
  output out_3
);

  wire and_1_out, and_2_out, nor_1_out, not_1_out;

  not not_1 (not_1_out, in_1);
  and and_1 (and_1_out, in_1, in_2);
  and and_2 (and_2_out, in_2, not_1_out);
  nor nor_1 (nor_1_out, and_1_out, out_3);
  nor nor_2 (out_3, nor_1_out, and_2_out);
endmodule

module _4bit_REGISTER (
  input  DATA_3,
  input  DATA_2,
  input  DATA_1,
  input  DATA_0,
  input  STORE,
  output out_6,
  output out_7,
  output out_8,
  output out_9
);

  Data_Latch data_latch_1 (.in_1(DATA_3), .in_2(STORE), .out_3(out_6));
  Data_Latch data_latch_2 (.in_1(DATA_2), .in_2(STORE), .out_3(out_7));
  Data_Latch data_latch_3 (.in_1(DATA_1), .in_2(STORE), .out_3(out_8));
  Data_Latch data_latch_4 (.in_1(DATA_0), .in_2(STORE), .out_3(out_9));
endmodule

module ASYNC_REGISTER (
  input  in_1,
  input  in_2,
  input  in_3,
  input  in_4,
  input  in_5,
  output out_6,
  output out_7,
  output out_8,
  output out_9
);

  wire n4bit_register_2_out_6, n4bit_register_2_out_7, n4bit_register_2_out_8, n4bit_register_2_out_9;

  _4bit_REGISTER u_4bit_register_1 (
    .DATA_3(in_1), .DATA_2(in_2), .DATA_1(in_3), .DATA_0(in_4), .STORE(in_5), .out_6(out_6), .out_7(out_7),
    .out_8(out_8), .out_9(out_9));
  _4bit_REGISTER u_4bit_register_2 (
    .out_6(n4bit_register_2_out_6), .out_7(n4bit_register_2_out_7), .out_8(n4bit_register_2_out_8),
    .out_9(n4bit_register_2_out_9));  // open: DATA_3, DATA_2, DATA_1, DATA_0, STORE
endmodule

module Data_FLIP_FLOP (
  input  DATA,
  input  in_2,
  output out_3
);

  wire not_1_out;

  not not_1 (not_1_out, in_2);
  Data_Latch data_latch_1 (.in_1(DATA), .in_2(not_1_out), .out_3(in_2));
  Data_Latch data_latch_2 (.in_1(in_2), .in_2(in_2), .out_3(out_3));

  // Notes on the sheet:
  //   CLOCK
endmodule

module _1bit_REGISTER (
  input  in_1,
  input  in_2,
  input  in_3,
  output out_4
);

  wire and_1_out, and_2_out, not_1_out, or_1_out;

  not not_1 (not_1_out, in_2);
  and and_1 (and_1_out, out_4, not_1_out);
  and and_2 (and_2_out, in_2, in_1);
  or or_1 (or_1_out, and_1_out, and_2_out);
  Data_FLIP_FLOP data_flip_flop_1 (.DATA(or_1_out), .in_2(in_3), .out_3(out_4));
endmodule

module _4bit_REGISTER_0 (
  input  in_1,
  input  in_2,
  input  in_3,
  input  in_4,
  input  in_5,
  input  in_6,
  output out_7,
  output out_8,
  output out_9,
  output out_10
);

  _1bit_REGISTER u_1bit_register_1 (.in_1(in_1), .in_2(in_5), .in_3(in_6), .out_4(out_7));
  _1bit_REGISTER u_1bit_register_2 (.in_1(in_2), .in_2(in_5), .in_3(in_6), .out_4(out_8));
  _1bit_REGISTER u_1bit_register_3 (.in_1(in_3), .in_2(in_5), .in_3(in_6), .out_4(out_9));
  _1bit_REGISTER u_1bit_register_4 (.in_1(in_4), .in_2(in_5), .in_3(in_6), .out_4(out_10));
endmodule
